// Logisim project capstone-circuit.circ as structural Verilog: 10 circuits, main circuit main
module main (
  input  Enable,
  input  Clear,
  input  Clock,
  input  Clear_2,
  input  Chip_Select,
  input  Clock_2,
  input  Load_Data,
  input  WE,
  output [7:0] IR_Current_Address,
  output [7:0] IR_Current_Instruction,
  output [7:0] ALU_Output,
  output CF,
  output SF,
  output ZF,
  output [7:0] R1,
  output [7:0] R2,
  output [7:0] R3,
  output [7:0] R4
);

  wire clock_1_fetch, clock_1_write, control_store_1_first_bit;
  wire [1:0] register_file_1_p3, register_file_1_p10;
  wire [5:0] control_store_1__6_bit_opcode;
  wire [7:0] control_store_1__8_bit_imm_value, multiplexer_1_out, multiplexer_2_out, multiplexer_3_out,
       register_file_1_p11, register_file_1_p12;
  wire [15:0] ram_1_data;

  Clock clock_1 (.Clock(Clock), .Fetch(clock_1_fetch), .Write(clock_1_write));  // open: Execute
  Multiplexer #(.width(8), .enable("false")) multiplexer_1 (
    .in0(ALU_Output), .out(multiplexer_1_out), .sel(clock_1_write));  // open: in1
  // Register_File register_file_1: pin names not known; wires that end beside it: WE, multiplexer_1_out, register_file_1_p3, R1, clock_1_write, R2, R3, register_file_1_p3, R4, register_file_1_p10, register_file_1_p11, register_file_1_p12
  Control_Store control_store_1 (
    .Clear(Clear), .Enable(Enable), .Clock(clock_1_fetch), ._8_Bit_Addr(IR_Current_Address),
    ._8_bit_inst(IR_Current_Instruction), ._8_bit_imm_value(control_store_1__8_bit_imm_value),
    .r1(register_file_1_p3), .r2(register_file_1_p10), .First_Bit(control_store_1_first_bit),
    ._6_Bit_Opcode(control_store_1__6_bit_opcode), ._16_Bit_Data(ram_1_data));
  Multiplexer #(.width(8), .enable("false")) multiplexer_2 (
    .in0(register_file_1_p11), .in1(control_store_1__8_bit_imm_value), .out(multiplexer_2_out),
    .sel(control_store_1_first_bit));
  Multiplexer #(.width(8), .enable("false")) multiplexer_3 (
    .in0(register_file_1_p12), .in1(control_store_1__8_bit_imm_value), .out(multiplexer_3_out),
    .sel(control_store_1_first_bit));
  ALU alu_1 (
    .CF(CF), .A(multiplexer_2_out), .B(multiplexer_3_out), .Opcode(control_store_1__6_bit_opcode),
    .Result(ALU_Output), .ZF(ZF), .SF(SF));
  RAM #(.dataWidth(16)) ram_1 (
    .addr(IR_Current_Address), .data(ram_1_data), .sel(Chip_Select), .clk(Clock_2), .ld(Load_Data),
    .clr(Clear_2));

  // Notes on the sheet:
  //   8-Bit CPU, created by Nick Greiner and Isaac Parker
  //   CSC-2410 Capstone Project
endmodule

module Logical_Unit (
  input  in_1,
  input  in_2,
  input  in_3,
  input  in_4,
  input  in_5,
  output out_6,
  output out_7,
  output out_8,
  output out_9,
  output out_10
);

  wire A___B_out, AB_out, Not_B_out;

  and AB (AB_out, in_1, in_2);
  or A___B (A___B_out, in_1, in_2);
  not Not_B (Not_B_out, in_2);
  and and_1 (out_6, AB_out, in_3);
  and and_2 (out_7, A___B_out, in_4);
  and and_3 (out_8, Not_B_out, in_5);

  assign out_9 = in_1;
  assign out_10 = in_2;
endmodule

module Full_Adder (
  input  in_1,
  input  in_2,
  input  in_3,
  input  in_4,
  output out_5,
  output out_6
);

  wire and_1_out, and_2_out, xor_1_out, xor_2_out;

  and and_1 (and_1_out, in_4, in_3, in_2);
  or or_1 (out_6, and_1_out, and_2_out);
  xor xor_1 (xor_1_out, in_2, in_3);
  and and_2 (and_2_out, in_4, xor_1_out, in_1);
  xor xor_2 (xor_2_out, in_1, xor_1_out);
  and and_3 (out_5, xor_2_out, in_4);
endmodule

module Decoder (
  input  in_1,
  input  in_2,
  output out_3,
  output out_4,
  output out_5,
  output out_6
);

  wire not_1_out, not_2_out;

  not not_1 (not_1_out, in_1);
  not not_2 (not_2_out, in_2);
  and and_1 (out_3, not_1_out, not_2_out);
  and and_2 (out_4, not_1_out, in_2);
  and and_3 (out_5, in_1, not_2_out);
  and and_4 (out_6, in_1, in_2);
endmodule

module _1bit_ALU (
  input  INVA,
  input  A,
  input  Carry_In,
  input  ENA,
  input  B,
  input  ENB,
  input  F0,
  input  F1,
  output Output,
  output Carry_Out
);

  wire and_1_out, and_2_out, DC_out_3, DC_out_4, DC_out_5, DC_out_6, FA_out_5, LU_out_6, LU_out_7, LU_out_8,
       LU_out_9, LU_out_10, xor_1_out;

  and and_1 (and_1_out, A, ENA);
  xor xor_1 (xor_1_out, INVA, and_1_out);
  and and_2 (and_2_out, B, ENB);
  Logical_Unit LU (
    .in_1(xor_1_out), .in_2(and_2_out), .out_6(LU_out_6), .out_7(LU_out_7), .out_8(LU_out_8),
    .out_9(LU_out_9), .out_10(LU_out_10), .in_3(DC_out_3), .in_4(DC_out_4), .in_5(DC_out_5));
  Decoder DC (.out_3(DC_out_3), .out_4(DC_out_4), .out_5(DC_out_5), .out_6(DC_out_6), .in_1(F0), .in_2(F1));
  Full_Adder FA (
    .in_2(LU_out_10), .in_3(LU_out_9), .in_4(DC_out_6), .in_1(Carry_In), .out_5(FA_out_5), .out_6(Carry_Out));
  or or_1 (Output, LU_out_6, LU_out_7, LU_out_8, FA_out_5);
endmodule

module ALU (
  input  [5:0] Opcode,
  input  [7:0] A,
  input  [7:0] B,
  output [7:0] Result,
  output SF,
  output ZF,
  output CF
);

  wire n1bit_alu_1_carry_out, n1bit_alu_2_carry_out, n1bit_alu_3_carry_out, n1bit_alu_4_carry_out,
       n1bit_alu_5_carry_out, n1bit_alu_6_carry_out, n1bit_alu_7_carry_out, not_1_out, not_2_out, not_3_out,
       not_4_out, not_5_out, not_6_out, not_7_out, not_8_out;

  _1bit_ALU u_1bit_alu_1 (
    .INVA(Opcode[1]), .A(A[0]), .ENA(Opcode[3]), .B(B[0]), .ENB(Opcode[2]), .F0(Opcode[5]), .F1(Opcode[4]),
    .Output(Result[0]), .Carry_Out(n1bit_alu_1_carry_out), .Carry_In(Opcode[0]));
  _1bit_ALU u_1bit_alu_2 (
    .INVA(Opcode[1]), .A(A[1]), .ENA(Opcode[3]), .B(B[1]), .ENB(Opcode[2]), .F0(Opcode[5]), .F1(Opcode[4]),
    .Output(Result[1]), .Carry_Out(n1bit_alu_2_carry_out), .Carry_In(n1bit_alu_1_carry_out));
  _1bit_ALU u_1bit_alu_3 (
    .INVA(Opcode[1]), .A(A[2]), .ENA(Opcode[3]), .B(B[2]), .ENB(Opcode[2]), .F0(Opcode[5]), .F1(Opcode[4]),
    .Output(Result[2]), .Carry_Out(n1bit_alu_3_carry_out), .Carry_In(n1bit_alu_2_carry_out));
  _1bit_ALU u_1bit_alu_4 (
    .INVA(Opcode[1]), .A(A[3]), .ENA(Opcode[3]), .B(B[3]), .ENB(Opcode[2]), .F0(Opcode[5]), .F1(Opcode[4]),
    .Output(Result[3]), .Carry_Out(n1bit_alu_4_carry_out), .Carry_In(n1bit_alu_3_carry_out));
  _1bit_ALU u_1bit_alu_5 (
    .INVA(Opcode[1]), .A(A[4]), .ENA(Opcode[3]), .B(B[4]), .ENB(Opcode[2]), .F0(Opcode[5]), .F1(Opcode[4]),
    .Output(Result[4]), .Carry_Out(n1bit_alu_5_carry_out), .Carry_In(n1bit_alu_4_carry_out));
  _1bit_ALU u_1bit_alu_6 (
    .INVA(Opcode[1]), .A(A[5]), .ENA(Opcode[3]), .B(B[5]), .ENB(Opcode[2]), .F0(Opcode[5]), .F1(Opcode[4]),
    .Output(Result[5]), .Carry_Out(n1bit_alu_6_carry_out), .Carry_In(n1bit_alu_5_carry_out));
  _1bit_ALU u_1bit_alu_7 (
    .INVA(Opcode[1]), .A(A[6]), .ENA(Opcode[3]), .B(B[6]), .ENB(Opcode[2]), .F0(Opcode[5]), .F1(Opcode[4]),
    .Output(Result[6]), .Carry_Out(n1bit_alu_7_carry_out), .Carry_In(n1bit_alu_6_carry_out));
  _1bit_ALU u_1bit_alu_8 (
    .INVA(Opcode[1]), .A(A[7]), .ENA(Opcode[3]), .B(B[7]), .ENB(Opcode[2]), .F0(Opcode[5]), .F1(Opcode[4]),
    .Output(Result[7]), .Carry_Out(CF), .Carry_In(n1bit_alu_7_carry_out));
  not not_1 (not_1_out, Result[4]);
  not not_2 (not_2_out, Result[5]);
  not not_3 (not_3_out, Result[7]);
  not not_4 (not_4_out, Result[6]);
  and and_1 (ZF, not_3_out, not_4_out, not_2_out, not_1_out, not_8_out, not_6_out, not_5_out, not_7_out);
  not not_5 (not_5_out, Result[1]);
  not not_6 (not_6_out, Result[2]);
  not not_7 (not_7_out, Result[0]);
  not not_8 (not_8_out, Result[3]);

  assign SF = Result[7];
endmodule

module Register_File (
  input  WE,
  input  Clock,
  input  [1:0] Sr0,
  input  [1:0] Sw,
  input  [1:0] Sr1,
  input  [7:0] Data_In,
  output [7:0] Data_Out_0,
  output [7:0] Data_Out_1,
  output [7:0] R1,
  output [7:0] R2,
  output [7:0] R3,
  output [7:0] R4
);

  wire demultiplexer_1_out0, demultiplexer_1_out1, demultiplexer_1_out2, demultiplexer_1_out3;

  Demultiplexer #(.select(2), .enable("false")) demultiplexer_1 (
    .out0(demultiplexer_1_out0), .out1(demultiplexer_1_out1), .out2(demultiplexer_1_out2),
    .out3(demultiplexer_1_out3), .in(Clock), .sel(Sw));
  Register #(.trigger("falling")) register_1 (.D(Data_In), .en(WE), .Q(R1), .clk(demultiplexer_1_out0));  // open: clr
  Register #(.trigger("falling")) register_2 (.D(Data_In), .en(WE), .Q(R2), .clk(demultiplexer_1_out1));  // open: clr
  Register #(.trigger("falling")) register_3 (.D(Data_In), .en(WE), .Q(R3), .clk(demultiplexer_1_out2));  // open: clr
  Register #(.trigger("falling")) register_4 (.D(Data_In), .en(WE), .Q(R4), .clk(demultiplexer_1_out3));  // open: clr
  Multiplexer #(.select(2), .width(8), .enable("false")) multiplexer_1 (
    .in0(R1), .in1(R2), .in2(R3), .in3(R4), .out(Data_Out_0), .sel(Sr0));
  Multiplexer #(.select(2), .width(8), .enable("false")) multiplexer_2 (
    .in0(R1), .in1(R2), .in2(R3), .in3(R4), .out(Data_Out_1), .sel(Sr1));
endmodule

module PC_IR (
  input  Clear,
  input  enable,
  input  Clock,
  input  [15:0] data_in,
  output [7:0] addr_out,
  output [7:0] instruction,
  output [7:0] immediate_value
);

  wire [7:0] adder_1_out;

  Register PC (.D(adder_1_out), .en(enable), .Q(addr_out), .clk(Clock), .clr(Clear));
  Register #(.width(16)) IR (.D(data_in), .en(enable), .Q({instruction, immediate_value}), .clk(Clock), .clr(Clear));
  Adder adder_1 (.a(8'h1), .b(addr_out), .out(adder_1_out), .cin(1'b0));  // open: cout
endmodule

module Control_Store (
  input  Clear,
  input  Enable,
  input  [15:0] _16_Bit_Data,
  input  Clock,
  output [7:0] _8_Bit_Addr,
  output [7:0] _8_bit_inst,
  output [7:0] _8_bit_imm_value,
  output First_Bit,
  output [1:0] r1,
  output [1:0] r2,
  output [5:0] _6_Bit_Opcode
);

  wire and_1_out, and_2_out, and_3_out, and_4_out, and_5_out, and_6_out, and_8_out, and_9_out, not_2_out,
       not_3_out, not_4_out, not_5_out, not_6_out, not_7_out, not_8_out, not_9_out, not_10_out, not_11_out,
       not_12_out, not_13_out;

  PC_IR pc_ir_1 (
    .Clear(Clear), .enable(Enable), .Clock(Clock), .instruction(_8_bit_inst), .addr_out(_8_Bit_Addr),
    .data_in(_16_Bit_Data), .immediate_value(_8_bit_imm_value));
  not not_1 (_6_Bit_Opcode[5], _8_bit_inst[6]);
  not not_2 (not_2_out, _8_bit_inst[6]);
  not not_3 (not_3_out, _8_bit_inst[6]);
  not not_4 (not_4_out, _8_bit_inst[4]);
  not not_5 (not_5_out, _8_bit_inst[5]);
  not not_6 (not_6_out, _8_bit_inst[6]);
  not not_7 (not_7_out, _8_bit_inst[6]);
  not not_8 (not_8_out, _8_bit_inst[5]);
  not not_9 (not_9_out, _8_bit_inst[6]);
  not not_10 (not_10_out, _8_bit_inst[6]);
  not not_11 (not_11_out, _8_bit_inst[5]);
  not not_12 (not_12_out, _8_bit_inst[4]);
  not not_13 (not_13_out, _8_bit_inst[6]);
  or or_1 (_6_Bit_Opcode[4], not_2_out, _8_bit_inst[4]);
  and and_1 (and_1_out, not_3_out, not_4_out);
  and and_2 (and_2_out, _8_bit_inst[5], _8_bit_inst[4]);
  or or_2 (_6_Bit_Opcode[3], and_1_out, and_2_out, and_3_out);
  and and_3 (and_3_out, _8_bit_inst[6], not_5_out);
  and and_4 (and_4_out, not_6_out, _8_bit_inst[4]);
  and and_5 (and_5_out, not_7_out, _8_bit_inst[5]);
  or or_3 (_6_Bit_Opcode[2], and_4_out, and_5_out, and_6_out);
  and and_6 (and_6_out, _8_bit_inst[6], not_8_out);
  and and_7 (_6_Bit_Opcode[1], not_9_out, _8_bit_inst[4]);
  and and_8 (and_8_out, not_10_out, not_11_out, not_12_out);
  or or_4 (_6_Bit_Opcode[0], and_8_out, and_9_out);
  and and_9 (and_9_out, not_13_out, _8_bit_inst[5], _8_bit_inst[4]);

  assign First_Bit = _8_bit_inst[7];
  assign r1 = _8_bit_inst[3:2];
  assign r2 = _8_bit_inst[1:0];

  // Notes on the sheet:
  //   Load RAM with program
  //   Enable the PC_IR chip
  //   Each time you clock 0-->1-->0
  //   Next instruction is loaded 
endmodule

module Clock (
  input  Clock,
  output Execute,
  output Write,
  output Fetch
);

  D_Flip_Flop d_ff_1 (.clk(Clock), .D(1'b1), .Q(Fetch), .reset(Execute));  // open: Qn, preset, en
  D_Flip_Flop d_ff_2 (.clk(Clock), .D(Fetch), .Q(Execute), .reset(Write));  // open: Qn, preset, en
  D_Flip_Flop d_ff_3 (.clk(Clock), .D(Execute), .Q(Write), .reset(Fetch));  // open: Qn, preset, en
endmodule
